# Fritzing sketch monk-circuit (saved by Fritzing 0.9.3b)
breadboards: 1

parts:
  P1 = POT [package=pot_mammoth]
  P2 = POT [package=pot_mammoth]
  U3 = POT [package=pot_mammoth]
  U4 = POT [package=pot_mammoth]
  U5 = POT [package=pot_mammoth]
  U6 = POT [package=pot_mammoth]
  Arduino = Arduino Uno (Rev3) - ICSP

nets:
  N1: P1.S, P2.S, U3.S, U4.S, U5.S, U6.S, Arduino.GND
  N2: P1.A, Arduino.A0
  N3: P1.E, P2.E, U3.E, U4.E, U5.E, U6.E, Arduino.5V
  N4: P2.A, Arduino.A1
  N5: U3.A, Arduino.A2
  N6: U4.A, Arduino.A4/SDA
  N7: U5.A, Arduino.A5/SCL
  N8: U6.A, Arduino.A3

notes:
  Arduino Uno
  USB connection sends the readings of the six Potentiometers to the computer. The PureData patch will collect those readings and utilize them to produce some sound.
  The Potentiometers' connection to the Arduino is pretty straightforward.
  It can be set up on a breadboard in about 5 minutes.
